# Fritzing sketch Receiver (saved by Fritzing 0.9.3b)
circuit board: 10cm x 6cm

parts:
  Part1 = Arduino Nano (Rev3.0)
  HC-1 = HC-12 Module
  Antenna1 = HC-12 Antenna
  R10 = Resistor [tolerance=±5% resistance=5.1m package=THT]
  R11 = Resistor [tolerance=±5% resistance=10m package="0603 [SMD]"]
  C1 = Ceramic Capacitor [capacitance="100 nF" package="0805 [SMD, multilayer]"]  # not connected
  DC_to_DC_converter_12V_to_5V = RioRand LM2596
  U1 = LIPO-1000mAh [part_number=7.4V package=lipo-1000]
  Battary_Charger = USB LiPoly Charger  # not connected
  J1 = Basic Servo
  J2 = Basic Servo
  J3 = Basic Servo

nets:
  N1: Part1.D1/TX, HC-1.RXD
  N2: Part1.D0/RX, HC-1.TXD
  N3: Part1.D2, J3.pulse
  N4: Part1.D3, J2.pulse
  N5: Part1.D4, J1.pulse
  GND: Part1.GND, HC-1.GND, R10.Pin_0, R11.Pin_1, DC_to_DC_converter_12V_to_5V.Pin_3
  N6: Part1.A7, R11.Pin_0
  VCC: HC-1.VCC, DC_to_DC_converter_12V_to_5V.Pin_2, J2.vcc, J3.vcc
  N7: HC-1.ANT, Antenna1.ANT
  N8: U1.-, J1.gnd

custom parts:
  HC-12 Module: HC-12 433Mhz Module
  HC-12 Antenna: Antenna for HC-12 433Mhz Module
