# Fritzing sketch Transmitter (saved by Fritzing 0.9.3b)

parts:
  Part1 = Arduino Nano (Rev3.0)
  HC-1 = HC-12 Module
  Antenna1 = HC-12 Antenna
  Trim1 = Rotary Potentiometer (Large) [maximum_resistance=100kΩ package=THT]
  Trim2 = Rotary Potentiometer (Large) [maximum_resistance=100kΩ package=THT]
  Grove1 = Grove OLED 128x96
  DC_to_DC_converter_12V_to_5V = RioRand LM2596
  U1 = LIPO-1000mAh [part_number=7.4V package=lipo-1000]  # not connected
  Battary_Charger = USB LiPoly Charger  # not connected
  CD4048B1 = CD4048B [part_number=CD4048B package="DIP (Dual Inline) [THT]"]
  R1-R8 = Resistor [tolerance=±5% resistance=10k package=THT]
  Key1 = Pushbutton [package="[SMD]"]
  Key2 = Pushbutton [package="[SMD]"]
  Key3 = Pushbutton [package="[THT]"]
  Key4 = Pushbutton [package="[THT]"]
  R2 = Resistor [tolerance=±5% resistance=10k package=THT]
  R3 = Resistor [tolerance=±5% resistance=10k package=THT]
  R4 = Resistor [tolerance=±5% resistance=10k package=THT]
  R5 = Resistor [tolerance=±5% resistance=10k package=THT]  # not connected
  R6 = Resistor [tolerance=±5% resistance=10k package=THT]  # not connected
  R7 = Resistor [tolerance=±5% resistance=10k package=THT]  # not connected
  R8 = Resistor [tolerance=±5% resistance=10k package=THT]  # not connected
  Key5 = Pushbutton [package="[SMD]"]
  Key6 = Pushbutton [package="[SMD]"]
  Key7 = Pushbutton [package="[THT]"]
  Key8 = Pushbutton [package="[THT]"]
  C1 = Capacitor [package=cap-pth-5mm]
  C2 = Capacitor [package=cap-pth-5mm]

nets:
  N1: Part1.D2, HC-1.RXD
  N2: Part1.D3, HC-1.SET, HC-1.TXD
  N3: Part1.D4, CD4048B1.Ka
  N4: Part1.D5, CD4048B1.Kc
  N5: Part1.D6, CD4048B1.H
  GND: Part1.GND, HC-1.GND, CD4048B1.VSS
  N6: Part1.A5, Grove1.SCL
  N7: Part1.A4, Grove1.SDA
  N8: Part1.A2, Trim1.wiper, C1.1
  N9: Part1.A1, Trim2.wiper, C2.1
  N10: HC-1.ANT, Antenna1.ANT
  N11: Trim1.leg2, C1.2
  N12: Trim2.leg1, CD4048B1.VDD, Key1.Pin_3, Key1.Pin_4, Key2.Pin_3, Key2.Pin_4, Key3.Pin_3, Key8.Pin_3, Key8.Pin_4
  N13: Trim2.leg2, C2.2
  N14: Grove1.GND, DC_to_DC_converter_12V_to_5V.Pin_3
  N15: Grove1.VCC, DC_to_DC_converter_12V_to_5V.Pin_2
  N16: CD4048B1.J, R1-R8.Pin_0, Key1.Pin_1, Key1.Pin_2
  N17: CD4048B1.G, Key2.Pin_1, Key2.Pin_2, R2.Pin_0
  N18: CD4048B1.F, Key3.Pin_1, R3.Pin_0
  N19: CD4048B1.E, Key4.Pin_1, Key4.Pin_2, R4.Pin_0
  N20: CD4048B1.Kb, Key5.Pin_1, Key5.Pin_2
  N21: CD4048B1.C, Key6.Pin_1, Key6.Pin_2
  N22: CD4048B1.B, Key7.Pin_1
  N23: CD4048B1.A, Key8.Pin_1

custom parts:
  HC-12 Module: HC-12 433Mhz Module
  HC-12 Antenna: Antenna for HC-12 433Mhz Module
